// Logisim project AND.circ as structural Verilog: 1 circuit, main circuit main
module main (
  input  [7:0] a,
  input  [7:0] b,
  output [7:0] out_3
);

  wire and_1_out, and_2_out, and_3_out, and_4_out, and_5_out, and_6_out, and_7_out, and_8_out;

  and and_1 (and_1_out, a[0], b[0]);
  and and_2 (and_2_out, a[1], b[1]);
  and and_3 (and_3_out, a[2], b[2]);
  and and_4 (and_4_out, a[3], b[3]);
  and and_5 (and_5_out, a[4], b[4]);
  and and_6 (and_6_out, a[5], b[5]);
  and and_7 (and_7_out, a[6], b[6]);
  and and_8 (and_8_out, a[7], b[7]);
  Juntor juntor_1 (
    .in_1(and_1_out), .in_2(and_2_out), .in_3(and_3_out), .in_4(and_4_out), .in_5(and_5_out),
    .in_6(and_6_out), .in_7(and_7_out), .in_8(and_8_out), .out_9(out_3));
endmodule
