// Logisim project Banco de Registradores.circ as structural Verilog: 1 circuit, main circuit Banco de Registradores
module Banco_de_Registradores (
  input  EscReg,
  input  [1:0] Reg__1,
  input  [1:0] Reg__2,
  input  [7:0] Dado_de_Escrita,
  input  \Clear__Quando_em_1__o_valor_do_pino_será_0_assicronamente ,
  input  Clock__Valor_atualizado_ao_gatilho,
  output [7:0] Dado_lido__1,
  output [7:0] Dado_lido__2
);

  wire demultiplexer_1_out0, demultiplexer_1_out1, demultiplexer_1_out2, demultiplexer_1_out3;
  wire [7:0] demultiplexer_2_out0, demultiplexer_2_out1, demultiplexer_2_out2, demultiplexer_2_out3,
       Reg__1_q, Reg__2_q, Reg__3_q, Reg__4_q;

  Demultiplexer #(.select(2)) demultiplexer_1 (
    .out0(demultiplexer_1_out0), .out1(demultiplexer_1_out1), .out2(demultiplexer_1_out2),
    .out3(demultiplexer_1_out3), .in(EscReg), .sel(Reg__1), .en(EscReg));
  Demultiplexer #(.select(2), .width(8)) demultiplexer_2 (
    .out0(demultiplexer_2_out0), .out1(demultiplexer_2_out1), .out2(demultiplexer_2_out2),
    .out3(demultiplexer_2_out3), .in(Dado_de_Escrita), .sel(Reg__1), .en(EscReg));
  Register u_Reg__1 (
    .D(demultiplexer_2_out0), .en(demultiplexer_1_out0), .Q(Reg__1_q),
    .clk(Clock__Valor_atualizado_ao_gatilho),
    .clr(\Clear__Quando_em_1__o_valor_do_pino_será_0_assicronamente ));
  Register u_Reg__2 (
    .D(demultiplexer_2_out1), .en(demultiplexer_1_out1), .Q(Reg__2_q),
    .clk(Clock__Valor_atualizado_ao_gatilho),
    .clr(\Clear__Quando_em_1__o_valor_do_pino_será_0_assicronamente ));
  Register Reg__3 (
    .D(demultiplexer_2_out2), .en(demultiplexer_1_out2), .Q(Reg__3_q),
    .clk(Clock__Valor_atualizado_ao_gatilho),
    .clr(\Clear__Quando_em_1__o_valor_do_pino_será_0_assicronamente ));
  Register Reg__4 (
    .D(demultiplexer_2_out3), .en(demultiplexer_1_out3), .Q(Reg__4_q),
    .clk(Clock__Valor_atualizado_ao_gatilho),
    .clr(\Clear__Quando_em_1__o_valor_do_pino_será_0_assicronamente ));
  Multiplexer #(.select(2), .width(8), .enable("false")) multiplexer_1 (
    .in0(Reg__1_q), .in1(Reg__2_q), .in2(Reg__3_q), .in3(Reg__4_q), .out(Dado_lido__1), .sel(Reg__1));
  Multiplexer #(.select(2), .width(8), .enable("false")) multiplexer_2 (
    .in0(Reg__1_q), .in1(Reg__2_q), .in2(Reg__3_q), .in3(Reg__4_q), .out(Dado_lido__2), .sel(Reg__2));
endmodule
