// Logisim project OR.circ as structural Verilog: 1 circuit, main circuit or
module \or  (
  input  [7:0] a,
  input  [7:0] b,
  output [7:0] out_3
);

  wire or_1_out, or_2_out, or_3_out, or_4_out, or_5_out, or_6_out, or_7_out, or_8_out;

  or or_1 (or_1_out, a[0], b[0]);
  or or_2 (or_2_out, a[1], b[1]);
  or or_3 (or_3_out, a[2], b[2]);
  or or_4 (or_4_out, a[3], b[3]);
  or or_5 (or_5_out, a[4], b[4]);
  or or_6 (or_6_out, a[5], b[5]);
  or or_7 (or_7_out, a[6], b[6]);
  or or_8 (or_8_out, a[7], b[7]);
  Juntor juntor_1 (
    .in_1(or_1_out), .in_2(or_2_out), .in_3(or_3_out), .in_4(or_4_out), .in_5(or_5_out), .in_6(or_6_out),
    .in_7(or_7_out), .in_8(or_8_out), .out_9(out_3));
endmodule
