// Logisim project Prototipo 002.circ as structural Verilog: 1 circuit, main circuit Prototipo 01
module Prototipo_01 (
  output [7:0] overflow_mult
);

  wire and_1_out, and_2_out, and_3_out, and_4_out, clock_1_out, multiplexer_1_out, or_1_out, or_2_out,
       or_3_out, Reset_out, UC_complememto_de_2, UC_dvc, UC_escmem, UC_escreg, UC_lermem, UC_memparareg,
       UC_ulafont, ula_8bits_1_overflow, ula_8bits_1_zero;
  wire [2:0] UC_ulaop1;
  wire [7:0] BD_registradores_dado_lido__1, BD_registradores_dado_lido__2, bit_extender_1_out,
       multiplexer_2_out, multiplexer_3_out, multiplexer_4_out, multiplexer_5_out, PC_q, ram_1_data,
       ram_2_data, register_1_q, Somador_2_out_3, Somador_out_3, ula_8bits_1_result;

  Multiplexer #(.enable("false")) multiplexer_1 (
    .in0(or_1_out), .in1(clock_1_out), .out(multiplexer_1_out), .sel(or_1_out));
  Clock clock_1 (.out(clock_1_out));
  Button Reset (.out(Reset_out));
  Register PC (.D(multiplexer_4_out), .en(or_1_out), .Q(PC_q), .clk(multiplexer_1_out), .clr(Reset_out));
  Somador Somador (.in_1(PC_q), .in_2(8'h1), .out_3(Somador_out_3));
  or or_1 (or_1_out, ram_1_data[0], ram_1_data[1], ram_1_data[2], ram_1_data[3], ram_1_data[4], ram_1_data[5], ram_1_data[6], ram_1_data[7]);
  RAM ram_1 (.addr(PC_q), .data(ram_1_data), .sel(1'b1), .clk(multiplexer_1_out), .ld(1'b1));  // open: clr
  and and_1 (and_1_out, ram_1_data[4], ram_1_data[5], ram_1_data[6], ram_1_data[7]);
  UNIDADE_DE_CONTROLE UC (
    .in_1(ram_1_data[7:4]), .DvC(UC_dvc), .MemParaReg(UC_memparareg), .EscReg(UC_escreg), .LerMem(UC_lermem),
    .EscMem(UC_escmem), .ULAOp1(UC_ulaop1), .complememto_de_2(UC_complememto_de_2), .ULAFont(UC_ulafont));
  assign bit_extender_1_out = {{4{1'b0}}, ram_1_data[3:0]};  // Bit_Extender bit_extender_1
  Banco_de_Registradores BD_registradores (
    .Reg__1(ram_1_data[3:2]), .Reg__2(ram_1_data[1:0]), .Dado_de_Escrita(multiplexer_5_out),
    .Dado_lido__1(BD_registradores_dado_lido__1), .Dado_lido__2(BD_registradores_dado_lido__2),
    .EscReg(UC_escreg), .Clock__Valor_atualizado_ao_gatilho(multiplexer_1_out),
    .\Clear__Quando_em_1__o_valor_do_pino_será_0_assicronamente (Reset_out));
  Multiplexer #(.width(8), .enable("false")) multiplexer_2 (
    .in0(bit_extender_1_out), .in1(8'h1), .out(multiplexer_2_out), .sel(and_3_out));
  Multiplexer #(.width(8), .enable("false")) multiplexer_3 (
    .in0(BD_registradores_dado_lido__2), .in1(register_1_q), .out(multiplexer_3_out), .sel(UC_ulafont));
  Register register_1 (.D(bit_extender_1_out), .Q(register_1_q), .clk(multiplexer_1_out), .clr(Reset_out));  // open: en
  Somador Somador_2 (.in_1(Somador_out_3), .in_2(multiplexer_2_out), .out_3(Somador_2_out_3));
  and and_2 (and_2_out, and_1_out, UC_dvc);
  and and_3 (and_3_out, ula_8bits_1_zero, UC_dvc);
  ULA_8bits ula_8bits_1 (
    .a(BD_registradores_dado_lido__1), .b(multiplexer_3_out), .result(ula_8bits_1_result),
    .Overflow(ula_8bits_1_overflow), .Complemento_de_2(UC_complememto_de_2), .ULA_Opcode(UC_ulaop1),
    .Zero(ula_8bits_1_zero), .carry_out_mult(overflow_mult));
  or or_2 (or_2_out, and_2_out, and_4_out, and_3_out);
  and and_4 (and_4_out, UC_dvc, ula_8bits_1_overflow);
  Multiplexer #(.width(8), .enable("false")) multiplexer_4 (
    .in0(Somador_out_3), .in1(Somador_2_out_3), .out(multiplexer_4_out), .sel(or_2_out));
  RAM #(.bus("separate")) ram_2 (
    .addr(ula_8bits_1_result), .din(BD_registradores_dado_lido__1), .data(ram_2_data), .str(UC_escmem),
    .sel(or_3_out), .clk(multiplexer_1_out), .ld(UC_lermem), .clr(Reset_out));
  or or_3 (or_3_out, UC_escmem, UC_lermem);
  Multiplexer #(.width(8), .enable("false")) multiplexer_5 (
    .in0(ula_8bits_1_result), .in1(ram_2_data), .out(multiplexer_5_out), .sel(UC_memparareg));

  // Notes on the sheet:
  //   Memoria de instruções
  //   ULA
  //   Memoria de Dados
endmodule
