// Logisim project Soma.circ as structural Verilog: 1 circuit, main circuit Soma
module Soma (
  input  a,
  input  b,
  input  Carry_in,
  output Soma,
  output Carry_out
);

  wire and_1_out, and_2_out, main_1_x;

  XOR_main main_1 (.a(a), .b(b), .x(main_1_x));
  and and_1 (and_1_out, Carry_in, main_1_x);
  and and_2 (and_2_out, b, a);
  XOR_main main_2 (.a(main_1_x), .b(Carry_in), .x(Soma));
  or or_1 (Carry_out, and_1_out, and_2_out);
endmodule
