// Logisim project XOR 8bits.circ as structural Verilog: 1 circuit, main circuit XOR 8bits
module XOR_8bits (
  input  [7:0] in_1,
  input  [7:0] in_2,
  output [7:0] out_3
);

  wire xor_1_out, xor_2_out, xor_3_out, xor_4_out, xor_5_out, xor_6_out, xor_7_out, xor_8_out;

  xor xor_1 (xor_1_out, in_1[0], in_2[0]);
  xor xor_2 (xor_2_out, in_1[1], in_2[1]);
  xor xor_3 (xor_3_out, in_1[2], in_2[2]);
  xor xor_4 (xor_4_out, in_1[3], in_2[3]);
  xor xor_5 (xor_5_out, in_1[4], in_2[4]);
  xor xor_6 (xor_6_out, in_1[5], in_2[5]);
  xor xor_7 (xor_7_out, in_1[6], in_2[6]);
  xor xor_8 (xor_8_out, in_1[7], in_2[7]);
  Juntor juntor_1 (
    .in_1(xor_1_out), .in_2(xor_2_out), .in_3(xor_3_out), .in_4(xor_4_out), .in_5(xor_5_out),
    .in_6(xor_6_out), .in_7(xor_7_out), .in_8(xor_8_out), .out_9(out_3));
endmodule
