// Logisim project deslocador de bits.circ as structural Verilog: 1 circuit, main circuit main
module main (
  input  [7:0] in_1,
  input  [7:0] in_2,
  output [7:0] out_3
);

  wire [1:0] main_1_out_3;
  wire [7:0] multiplexer_1_out;

  juntor_2bits_main main_1 (.in_1(in_2[0]), .in_2(in_2[1]), .out_3(main_1_out_3));
  Multiplexer #(.select(2), .width(8)) multiplexer_1 (
    .in0(8'h2), .in1(8'h4), .in2(8'h8), .in3(8'h10), .out(multiplexer_1_out), .sel(main_1_out_3));  // open: en
  Multiplier multiplier_1 (.a(in_1), .b(multiplexer_1_out), .out(out_3));  // open: cin, cout
endmodule
