// Logisim project juntor 2bits.circ as structural Verilog: 1 circuit, main circuit main
module main (
  input  in_1,
  input  in_2,
  output [1:0] out_3
);

  wire [1:0] bit_extender_1_out, bit_extender_2_out, shifter_1_out;

  assign bit_extender_1_out = {{1{1'b0}}, in_1};  // Bit_Extender bit_extender_1
  assign bit_extender_2_out = {{1{1'b0}}, in_2};  // Bit_Extender bit_extender_2
  Shifter #(.width(2)) shifter_1 (.in(bit_extender_2_out), .\dist (1'b1), .out(shifter_1_out));
  Adder #(.width(2)) adder_1 (.a(bit_extender_1_out), .b(shifter_1_out), .out(out_3));  // open: cin, cout
endmodule
