// Logisim project juntor.circ as structural Verilog: 1 circuit, main circuit Juntor
module Juntor (
  input  in_1,
  input  in_2,
  input  in_3,
  input  in_4,
  input  in_5,
  input  in_6,
  input  in_7,
  input  in_8,
  output [7:0] out_9
);

  wire adder_1_cout, adder_2_cout, adder_3_cout, adder_4_cout, adder_5_cout, adder_6_cout;
  wire [7:0] adder_1_out, adder_2_out, adder_3_out, adder_4_out, adder_5_out, adder_6_out,
       bit_extender_1_out, bit_extender_2_out, bit_extender_3_out, bit_extender_4_out, bit_extender_5_out,
       bit_extender_6_out, bit_extender_7_out, bit_extender_8_out, shifter_1_out, shifter_2_out,
       shifter_3_out, shifter_4_out, shifter_5_out, shifter_6_out, shifter_7_out, shifter_8_out;

  assign bit_extender_1_out = {{7{1'b0}}, in_1};  // Bit_Extender bit_extender_1
  assign bit_extender_2_out = {{7{1'b0}}, in_2};  // Bit_Extender bit_extender_2
  assign bit_extender_3_out = {{7{1'b0}}, in_3};  // Bit_Extender bit_extender_3
  assign bit_extender_4_out = {{7{1'b0}}, in_4};  // Bit_Extender bit_extender_4
  assign bit_extender_5_out = {{7{1'b0}}, in_5};  // Bit_Extender bit_extender_5
  assign bit_extender_6_out = {{7{1'b0}}, in_6};  // Bit_Extender bit_extender_6
  assign bit_extender_7_out = {{7{1'b0}}, in_7};  // Bit_Extender bit_extender_7
  assign bit_extender_8_out = {{7{1'b0}}, in_8};  // Bit_Extender bit_extender_8
  Shifter shifter_1 (.in(bit_extender_1_out), .\dist (3'b000), .out(shifter_1_out));
  Adder adder_1 (.a(shifter_1_out), .b(shifter_2_out), .out(adder_1_out), .cin(1'b0), .cout(adder_1_cout));
  Shifter shifter_2 (.in(bit_extender_2_out), .\dist (3'b001), .out(shifter_2_out));
  Shifter shifter_3 (.in(bit_extender_3_out), .\dist (3'b010), .out(shifter_3_out));
  Shifter shifter_4 (.in(bit_extender_4_out), .\dist (3'b011), .out(shifter_4_out));
  Shifter shifter_5 (.in(bit_extender_5_out), .\dist (3'b100), .out(shifter_5_out));
  Shifter shifter_6 (.in(bit_extender_6_out), .\dist (3'b101), .out(shifter_6_out));
  Shifter shifter_7 (.in(bit_extender_7_out), .\dist (3'b110), .out(shifter_7_out));
  Shifter shifter_8 (.in(bit_extender_8_out), .\dist (3'b111), .out(shifter_8_out));
  Adder adder_2 (.a(adder_1_out), .b(shifter_3_out), .out(adder_2_out), .cin(adder_1_cout), .cout(adder_2_cout));
  Adder adder_3 (.a(adder_2_out), .b(shifter_4_out), .out(adder_3_out), .cin(adder_2_cout), .cout(adder_3_cout));
  Adder adder_4 (.a(adder_3_out), .b(shifter_5_out), .out(adder_4_out), .cin(adder_3_cout), .cout(adder_4_cout));
  Adder adder_5 (.a(adder_4_out), .b(shifter_6_out), .out(adder_5_out), .cin(adder_4_cout), .cout(adder_5_cout));
  Adder adder_6 (.a(adder_5_out), .b(shifter_7_out), .out(adder_6_out), .cin(adder_5_cout), .cout(adder_6_cout));
  Adder adder_7 (.a(adder_6_out), .b(shifter_8_out), .out(out_9), .cin(adder_6_cout));  // open: cout
endmodule
