// Logisim project memoria de instruções.circ as structural Verilog: 1 circuit, main circuit main
module main (
);

  wire undriven_2, undriven_3, undriven_4, undriven_5;
  wire [7:0] ram_1_data, undriven;

  RAM ram_1 (.addr(undriven), .data(ram_1_data), .sel(undriven_2), .clk(undriven_3), .ld(undriven_4), .clr(undriven_5));

  // Notes on the sheet:
  //   8
  //   \
  //   8
  //   \
endmodule
