// Logisim project somador path.circ as structural Verilog: 1 circuit, main circuit Somador
module Somador (
  input  [7:0] in_1,
  input  [7:0] in_2,
  output [7:0] out_3
);

  wire [7:0] and_1_out, and_2_out, or_1_out, shifter_1_out, xor_1_out;

  assign xor_1_out = in_1 ^ in_2;  // XOR_Gate xor_1, 8 bits wide
  assign out_3 = xor_1_out ^ shifter_1_out;  // XOR_Gate xor_2, 8 bits wide
  assign and_1_out = xor_1_out & shifter_1_out;  // AND_Gate and_1, 8 bits wide
  assign and_2_out = in_2 & in_1;  // AND_Gate and_2, 8 bits wide
  assign or_1_out = and_1_out | and_2_out;  // OR_Gate or_1, 8 bits wide
  Shifter shifter_1 (.in(or_1_out), .\dist (3'b001), .out(shifter_1_out));
endmodule
