// Logisim project somador.circ as structural Verilog: 1 circuit, main circuit Somador
module Somador (
  input  carry_in,
  input  [7:0] a,
  input  [7:0] b,
  output [7:0] out_4,
  output carry_out
);

  wire soma_1_carry_out, soma_1_soma, soma_2_carry_out, soma_2_soma, soma_3_carry_out, soma_3_soma,
       soma_4_carry_out, soma_4_soma, soma_5_carry_out, soma_5_soma, soma_6_carry_out, soma_6_soma,
       soma_7_carry_out, soma_7_soma, soma_8_soma;

  Soma soma_1 (.a(a[0]), .b(b[0]), .Carry_in(carry_in), .Carry_out(soma_1_carry_out), .Soma(soma_1_soma));
  Soma soma_2 (.a(a[1]), .b(b[1]), .Carry_in(soma_1_carry_out), .Carry_out(soma_2_carry_out), .Soma(soma_2_soma));
  Soma soma_3 (.a(a[2]), .b(b[2]), .Carry_in(soma_2_carry_out), .Carry_out(soma_3_carry_out), .Soma(soma_3_soma));
  Soma soma_4 (.a(a[3]), .b(b[3]), .Carry_in(soma_3_carry_out), .Carry_out(soma_4_carry_out), .Soma(soma_4_soma));
  Soma soma_5 (.a(a[4]), .b(b[4]), .Carry_in(soma_4_carry_out), .Carry_out(soma_5_carry_out), .Soma(soma_5_soma));
  Soma soma_6 (.a(a[5]), .b(b[5]), .Carry_in(soma_5_carry_out), .Carry_out(soma_6_carry_out), .Soma(soma_6_soma));
  Soma soma_7 (.a(a[6]), .b(b[6]), .Carry_in(soma_6_carry_out), .Carry_out(soma_7_carry_out), .Soma(soma_7_soma));
  Soma soma_8 (.a(a[7]), .b(b[7]), .Carry_in(soma_7_carry_out), .Carry_out(carry_out), .Soma(soma_8_soma));
  Juntor juntor_1 (
    .in_1(soma_1_soma), .in_2(soma_2_soma), .in_3(soma_3_soma), .in_4(soma_4_soma), .in_5(soma_5_soma),
    .in_6(soma_6_soma), .in_7(soma_7_soma), .in_8(soma_8_soma), .out_9(out_4));
endmodule
