// Logisim project ula.circ as structural Verilog: 1 circuit, main circuit ULA 8bits
module ULA_8bits (
  input  [2:0] ULA_Opcode,
  input  Complemento_de_2,
  input  [7:0] a,
  input  [7:0] b,
  output Zero,
  output [7:0] result,
  output Overflow,
  output [7:0] carry_out_mult
);

  wire or_2_out;
  wire [7:0] adder_1_out, and_1_out, main_1_out_3, multiplexer_1_out, multiplier_1_out, not_1_out, or_1_out,
       xor_1_out;

  Multiplexer #(.width(8), .enable("false")) multiplexer_1 (
    .in0(b), .in1(not_1_out), .out(multiplexer_1_out), .sel(Complemento_de_2));
  assign not_1_out = ~b;  // NOT_Gate not_1, 8 bits wide
  Adder adder_1 (.a(a), .b(multiplexer_1_out), .out(adder_1_out), .cin(Complemento_de_2), .cout(Overflow));
  assign and_1_out = a & multiplexer_1_out;  // AND_Gate and_1, 8 bits wide
  assign or_1_out = a | multiplexer_1_out;  // OR_Gate or_1, 8 bits wide
  assign xor_1_out = a ^ multiplexer_1_out;  // XOR_Gate xor_1, 8 bits wide
  Multiplier multiplier_1 (.a(a), .b(multiplexer_1_out), .out(multiplier_1_out), .cout(carry_out_mult));  // open: cin
  deslocador_de_bits_main main_1 (.in_1(a), .in_2(multiplexer_1_out), .out_3(main_1_out_3));
  or or_2 (or_2_out, xor_1_out[0], xor_1_out[1], xor_1_out[2], xor_1_out[3], xor_1_out[4], xor_1_out[5], xor_1_out[6], xor_1_out[7]);
  Multiplexer #(.select(3), .width(8), .enable("false")) multiplexer_2 (
    .in0(adder_1_out), .in1(and_1_out), .in2(or_1_out), .in3(xor_1_out), .in4(multiplier_1_out),
    .in5(main_1_out_3), .in6(a), .in7(multiplexer_1_out), .out(result), .sel(ULA_Opcode));
  not not_2 (Zero, or_2_out);
endmodule
