// Logisim project unidade de controle.circ as structural Verilog: 1 circuit, main circuit UNIDADE DE CONTROLE
module UNIDADE_DE_CONTROLE (
  input  [3:0] in_1,
  output DvC,
  output MemParaReg,
  output EscReg,
  output LerMem,
  output EscMem,
  output [2:0] ULAOp1,
  output ULAFont,
  output complememto_de_2
);

  Multiplexer #(.select(4), .width(10), .enable("false")) multiplexer_1 (
    .in0(10'h4), .in1(10'h1e4), .in2(10'hee), .in3(10'hd0), .in4(10'h204), .in5(10'h100), .in6(10'h304),
    .in7(10'h61), .in8(10'h24), .in9(10'h44), .in10(10'h2e4), .in11(10'h1a4), .in12(10'h84), .in13(10'he4),
    .in14(10'h201), .in15(10'h1),
    .out({complememto_de_2, ULAFont, ULAOp1, EscMem, LerMem, EscReg, MemParaReg, DvC}), .sel(in_1));
endmodule
